# Fritzing sketch Heizstabsteuerung (saved by Fritzing 0.9.10b)
breadboards: 2

parts:
  MH-ET_LIVE_ESP32_DEVKIT1 = MH-ET LIVE ESP32 DEVKIT 38 pins
  U2 = mystery part, 3 pins [chip_label=DS18B20 part_number=DS18B20]
  LED3 = LED - 5mm [color="Green (565nm)" current=0.030 package="5 mm [THT]"]
  LED4 = LED - 5mm [color="Red (633nm)" current=0.030 package="5 mm [THT]"]
  R5 = Resistor [tolerance=±5% power=0.25 resistance=220 package=THT]
  R6 = Resistor [tolerance=±5% power=0.25 resistance=330 package=THT]
  U3 = mystery part, 3 pins [chip_label=DS18B20 part_number=DS18B20]
  U4 = mystery part, 3 pins [chip_label=DS18B20 part_number=DS18B20]
  M1 = AC-05-03
  J4 = female pin header, 6 pins [form="♀ (female)"]
  J5 = male pin header, 4 pins [form="♂ (male)"]
  Bauteil2 = I2C level shifter bidirectional
  R4 = Resistor [tolerance=±5% power=0.25 resistance=4.7k package=THT]
  J1 = male pin header, 2 pins [form="♂ (male)"]
  J2 = male pin header, 2 pins [form="♂ (male)"]
  J2_2 = male pin header, 2 pins [form="♂ (male)"]
  R7 = Resistor [tolerance=±5% power=0.25 resistance=10k package=THT]
  R8 = Resistor [tolerance=±5% power=0.25 resistance=10k package=THT]
  C1 = Electrolytic Capacitor [capacitance=10µF voltage=35V package="100 mil [THT, electrolytic]"]
  R9 = Resistor [tolerance=±5% power=0.25 resistance=10k package=THT]
  R10 = Resistor [tolerance=±5% power=0.25 resistance=10k package=THT]
  C2 = Electrolytic Capacitor [capacitance=10µF voltage=35V package="100 mil [THT, electrolytic]"]
  R11 = Resistor [tolerance=±5% power=0.25 resistance=10k package=THT]
  R12 = Resistor [tolerance=±5% power=0.25 resistance=10k package=THT]
  C3 = Electrolytic Capacitor [capacitance=10µF voltage=35V package="100 mil [THT, electrolytic]"]
  LED5 = LED - 5mm [color="Yellow (595nm)" current=0.030 package="5 mm [THT]"]
  R13 = Resistor [tolerance=±5% power=0.25 resistance=220 package=THT]

nets:
  N1: MH-ET_LIVE_ESP32_DEVKIT1.3V3, U2.pin3, U3.pin3, U4.pin3, J5.pin2, Bauteil2.LV, R4.Pin_1
  N2: MH-ET_LIVE_ESP32_DEVKIT1.SVP, J1.pin1
  N3: MH-ET_LIVE_ESP32_DEVKIT1.IO34, J2_2.pin1
  N4: MH-ET_LIVE_ESP32_DEVKIT1.IO35, J2.pin1
  N5: MH-ET_LIVE_ESP32_DEVKIT1.IO33, Bauteil2.LV4
  N6: MH-ET_LIVE_ESP32_DEVKIT1.IO25, U2.pin2, U3.pin2, U4.pin2, R4.Pin_0
  N7: MH-ET_LIVE_ESP32_DEVKIT1.5V, M1.pin_3, J4.pin6, Bauteil2.HV, R8.Pin_1
  N8: MH-ET_LIVE_ESP32_DEVKIT1.GND#64, U2.pin1, LED3.cathode, LED4.cathode, U3.pin1, U4.pin1, M1.pin_4, J4.pin5, J5.pin1, Bauteil2.GND, R7.Pin_0, C1.-, LED5.cathode
  N9: MH-ET_LIVE_ESP32_DEVKIT1.IO23, R5.Pin_0
  N10: MH-ET_LIVE_ESP32_DEVKIT1.IO22, J5.pin4
  N11: MH-ET_LIVE_ESP32_DEVKIT1.IO21, J5.pin3
  N12: MH-ET_LIVE_ESP32_DEVKIT1.IO19, R6.Pin_0
  N13: MH-ET_LIVE_ESP32_DEVKIT1.IO18, Bauteil2.LV1
  N14: MH-ET_LIVE_ESP32_DEVKIT1.IO17, Bauteil2.LV2
  N15: MH-ET_LIVE_ESP32_DEVKIT1.IO16, Bauteil2.LV3
  N16: MH-ET_LIVE_ESP32_DEVKIT1.IO4, R13.Pin_0
  N17: LED3.anode, R6.Pin_1
  N18: LED4.anode, R5.Pin_1
  N19: J4.pin2, Bauteil2.HV1
  N20: J4.pin3, Bauteil2.HV2
  N21: J4.pin4, Bauteil2.HV3
  N22: J1.pin2, R11.Pin_0, R12.Pin_1, C3.+
  N23: J2.pin2, R7.Pin_1, R8.Pin_0, C1.+
  N24: J2_2.pin2, R9.Pin_0, R10.Pin_1, C2.+
  N25: R10.Pin_0, C2.-
  N26: R12.Pin_0, C3.-
  N27: LED5.anode, R13.Pin_1

notes:
  Phasenüberwachung via STC013
  [+5V | Dout | GND | Aout]
  Schaltkanäle über Relais (CHN4|CHN3|CHN2|CHN1|DC-|DC+) (5V)
  Versorgung 5V für 400V SSR Trigger geschaltet über Relais
  Levelshift
  3.3V 5V
  Verbiundung zum 16x2
  LCD Panel (3.3V - 5V)
  [GND | vcc | sda | scl]
  L1*<_L2*<_L3*<
  TT,T_TT,T_TT,T°C
  Alarm:
  lost Power Lx Ly
  oder
  Alarm lost Power
  Lx Ly Lz
  GPIO 34 -> L1
  GPIO 35 -> L2
  GPIO 36 -> L3
  L2
  L3
  L1
  Phasenschaltung
  GPIO16 L1
  GPIO17 L2
  GPIO18 L3
  GPIO33 Lüfter
  Spannungsversorgung über AC-05-03 oder über PowerGuard

custom parts:
  MH-ET LIVE ESP32 DEVKIT 38 pins: http://mh.nodebb.com/topic/2/mh-et-live-esp32-devkit
  AC-05-03: AC-DC 220V to 5V Step-Down Power Supply Module
